# Fritzing sketch mkr-bh1750-sensor-circuit-diagram (saved by Fritzing 0.9.4)
breadboards: 1

parts:
  Part1 = Arduino MKR WiFi 1010
  BH1750FVI_Breakout1 = BH1750 (GY-302) Breakout Board [part_number=BH1750FVI]

nets:
  N1: Part1.D11_SDA, BH1750FVI_Breakout1.SDA
  N2: Part1.D12_SCL, BH1750FVI_Breakout1.SCL
  GND: Part1.GND, BH1750FVI_Breakout1.GND
  VCC: Part1.VCC, BH1750FVI_Breakout1.VCC

custom parts:
  Arduino MKR WiFi 1010: This is the newest version of the MKR 1000 WIFI, but with an ESP32 module on board made by U-BLOX.
  BH1750 (GY-302) Breakout Board: The ROHM Semiconductor BH1750FVI is a digital ambient light sensor for the I2C bus interface. The BH750FVI is able to detect a wide range of light intensities (1-65535 lux). The spectral range is similar to that of the human eye.
