# Fritzing sketch uno-bh1750-sensor-circuit-diagram (saved by Fritzing 0.9.4)
breadboards: 1

parts:
  Part2 = Arduino Uno (Rev3)
  BH1750FVI_Breakout1 = BH1750 (GY-302) Breakout Board [part_number=BH1750FVI]

nets:
  GND: Part2.GND, BH1750FVI_Breakout1.GND
  N1: Part2.A4/SDA, BH1750FVI_Breakout1.SDA
  N2: Part2.A5/SCL, BH1750FVI_Breakout1.SCL
  3V3: Part2.3V3, BH1750FVI_Breakout1.VCC

custom parts:
  BH1750 (GY-302) Breakout Board: The ROHM Semiconductor BH1750FVI is a digital ambient light sensor for the I2C bus interface. The BH750FVI is able to detect a wide range of light intensities (1-65535 lux). The spectral range is similar to that of the human eye.
