# Fritzing sketch esp32-bh1750-lux-sensor-circuit-diagram (saved by Fritzing 0.9.4)
breadboards: 1

parts:
  MCU1 = Wemos Lolin32lite
  BH1750FVI_Breakout1 = BH1750 (GY-302) Breakout Board [part_number=BH1750FVI]

nets:
  N1: MCU1.pin_13, BH1750FVI_Breakout1.GND
  N2: MCU1.pin_20, BH1750FVI_Breakout1.SDA
  N3: MCU1.pin_23, BH1750FVI_Breakout1.SCL
  N4: MCU1.pin_28, BH1750FVI_Breakout1.VCC

custom parts:
  Wemos Lolin32lite: Wemos Lolinlite32 wifi and bluetooth board based on the ESP-32 cpu, digital I/Os 19, analog inputs 6, clock 240mhz, Flash 4Mbytes, lipo battery charger (500ma connection broken out on breadboard but not pcb), usb.
  BH1750 (GY-302) Breakout Board: The ROHM Semiconductor BH1750FVI is a digital ambient light sensor for the I2C bus interface. The BH750FVI is able to detect a wide range of light intensities (1-65535 lux). The spectral range is similar to that of the human eye.
