# Fritzing sketch esp8266-bh1750-lux-sensor-circuit-diagram (saved by Fritzing 0.9.4)
breadboards: 1

parts:
  WeMos_D1_Mini1 = WeMos D1 Mini
  BH1750FVI_Breakout1 = BH1750 (GY-302) Breakout Board [part_number=BH1750FVI]

nets:
  3V3: WeMos_D1_Mini1.3V3, BH1750FVI_Breakout1.VCC
  N1: WeMos_D1_Mini1.D1, BH1750FVI_Breakout1.SCL
  N2: WeMos_D1_Mini1.D2, BH1750FVI_Breakout1.SDA
  N3: WeMos_D1_Mini1.G, BH1750FVI_Breakout1.GND

custom parts:
  BH1750 (GY-302) Breakout Board: The ROHM Semiconductor BH1750FVI is a digital ambient light sensor for the I2C bus interface. The BH750FVI is able to detect a wide range of light intensities (1-65535 lux). The spectral range is similar to that of the human eye.
